// Logisim project e2396273.circ as structural Verilog: 1 circuit, main circuit main
module main (
  input  O2,
  input  O1,
  input  O0,
  input  B1,
  input  B0,
  input  A1,
  input  A0,
  output L0,
  output L1,
  output L2,
  output S,
  output L3,
  output L4,
  output L5,
  output L6,
  output L7
);

  wire and_1_out, and_2_out, and_3_out, and_4_out, and_5_out, and_6_out, n3_to_8_decoder_74138_1_p13,
       n3_to_8_decoder_74138_2_p7, n3_to_8_decoder_74138_2_p8, n3_to_8_decoder_74138_2_p9,
       n3_to_8_decoder_74138_2_p10, n3_to_8_decoder_74138_2_p11, n3_to_8_decoder_74138_2_p12,
       n3_to_8_decoder_74138_2_p13, n3_to_8_decoder_74138_2_p14, n4_to_1_mux_x2_74153_1_p5,
       n4_to_1_mux_x2_74153_1_p6, n4_to_1_mux_x2_74153_1_p7, n4_to_1_mux_x2_74153_2_p5,
       n4_to_1_mux_x2_74153_2_p13, n4_to_1_mux_x2_74153_2_p14, n4_to_1_mux_x2_74153_3_p9,
       n4_to_1_mux_x2_74153_3_p13, n4_to_1_mux_x2_74153_4_p9, n4_to_1_mux_x2_74153_4_p13,
       n4_to_1_mux_x2_74153_4_p14, n4_to_1_mux_x2_74153_5_p12, n4_to_1_mux_x2_74153_5_p14,
       n4_to_1_mux_x2_74153_5_p15, n4_to_1_mux_x2_74153_6_p13, n4_to_1_mux_x2_74153_6_p14,
       n4_to_1_mux_x2_74153_7_p13, n4_to_1_mux_x2_74153_7_p14, n4_to_1_mux_x2_74153_8_p8, nand_1_out,
       nor_1_out, nor_2_out, not_1_out, not_2_out, not_3_out, not_4_out, not_5_out, or_1_out, or_2_out,
       or_3_out, or_4_out, xor_1_out, xor_2_out;

  not not_1 (not_1_out, O2);
  not not_2 (not_2_out, B0);
  not not_3 (not_3_out, B1);
  not not_4 (not_4_out, A0);
  not not_5 (not_5_out, A1);
  xor xor_1 (xor_1_out, A0, B0);
  and and_1 (and_1_out, A0, B0);
  and and_2 (and_2_out, not_4_out, not_5_out);
  and and_3 (and_3_out, A0, A1);
  or or_1 (or_1_out, A0, A1);
  or or_2 (or_2_out, A0, A1);
  and and_4 (and_4_out, not_4_out, not_5_out);
  nand nand_1 (nand_1_out, A0, A1);
  xor xor_2 (xor_2_out, A1, B1);
  and and_5 (and_5_out, A1, B1);
  nor nor_1 (nor_1_out, A1, B1);
  nor nor_2 (nor_2_out, A0, B0);
  and and_6 (and_6_out, not_4_out, not_5_out);
  // _4_to_1_MUX__x2___74153 #(.Facing("east")) 4_to_1_mux_x2_74153_1: pin names not known; wires that end beside it: xor_2_out, and_5_out, nor_1_out, not_1_out, n4_to_1_mux_x2_74153_1_p5, n4_to_1_mux_x2_74153_1_p6, n4_to_1_mux_x2_74153_1_p7
  // _4_to_1_MUX__x2___74153 #(.Facing("east")) 4_to_1_mux_x2_74153_2: pin names not known; wires that end beside it: B1, not_3_out, not_3_out, B1, n4_to_1_mux_x2_74153_2_p5, B1, B1, 1'b1, n4_to_1_mux_x2_74153_2_p5, A1, n4_to_1_mux_x2_74153_2_p5, and_1_out, n4_to_1_mux_x2_74153_2_p13, n4_to_1_mux_x2_74153_2_p14
  // _4_to_1_MUX__x2___74153 #(.Facing("east")) 4_to_1_mux_x2_74153_3: pin names not known; wires that end beside it: A1, and_3_out, and_2_out, not_5_out, or_1_out, A1, and_3_out, 1'b0, n4_to_1_mux_x2_74153_3_p9, B0, n4_to_1_mux_x2_74153_3_p9, B1, n4_to_1_mux_x2_74153_3_p13, S
  // _4_to_1_MUX__x2___74153 #(.Facing("east")) 4_to_1_mux_x2_74153_4: pin names not known; wires that end beside it: 1'b0, and_6_out, 1'b0, not_4_out, 1'b0, A0, not_4_out, 1'b1, n4_to_1_mux_x2_74153_4_p9, B0, n4_to_1_mux_x2_74153_4_p9, B1, n4_to_1_mux_x2_74153_4_p13, n4_to_1_mux_x2_74153_4_p14
  // _4_to_1_MUX__x2___74153 #(.Facing("east")) 4_to_1_mux_x2_74153_5: pin names not known; wires that end beside it: 1'b1, 1'b0, A1, or_2_out, or_2_out, and_4_out, not_5_out, nand_1_out, 1'b1, n4_to_1_mux_x2_74153_4_p9, B0, n4_to_1_mux_x2_74153_5_p12, B1, n4_to_1_mux_x2_74153_5_p14, n4_to_1_mux_x2_74153_5_p15
  // _3_to_8_decoder__74138 #(.Facing("east")) 3_to_8_decoder_74138_1: pin names not known; wires that end beside it: O0, O1, O2, 1'b1, 1'b0, 1'b0, n4_to_1_mux_x2_74153_2_p5, n4_to_1_mux_x2_74153_3_p9, n4_to_1_mux_x2_74153_4_p9, n4_to_1_mux_x2_74153_5_p12, n4_to_1_mux_x2_74153_1_p6, n4_to_1_mux_x2_74153_1_p5, n3_to_8_decoder_74138_1_p13, n3_to_8_decoder_74138_1_p13
  // _4_to_1_MUX__x2___74153 #(.Facing("east")) 4_to_1_mux_x2_74153_6: pin names not known; wires that end beside it: n4_to_1_mux_x2_74153_2_p13, n4_to_1_mux_x2_74153_3_p13, n4_to_1_mux_x2_74153_4_p14, 1'b0, n4_to_1_mux_x2_74153_1_p7, n4_to_1_mux_x2_74153_1_p7, n4_to_1_mux_x2_74153_1_p7, 1'b0, O2, O0, not_1_out, O1, n4_to_1_mux_x2_74153_6_p13, n4_to_1_mux_x2_74153_6_p14
  or or_3 (or_3_out, n4_to_1_mux_x2_74153_6_p13, n4_to_1_mux_x2_74153_6_p14);
  // _4_to_1_MUX__x2___74153 #(.Facing("east")) 4_to_1_mux_x2_74153_7: pin names not known; wires that end beside it: xor_1_out, xor_1_out, n4_to_1_mux_x2_74153_4_p13, n4_to_1_mux_x2_74153_5_p15, xor_1_out, and_1_out, nor_2_out, 1'b0, O2, O0, not_1_out, O1, n4_to_1_mux_x2_74153_7_p13, n4_to_1_mux_x2_74153_7_p14
  // _4_to_1_MUX__x2___74153 #(.Facing("east")) 4_to_1_mux_x2_74153_8: pin names not known; wires that end beside it: n4_to_1_mux_x2_74153_2_p14, 1'b0, n4_to_1_mux_x2_74153_5_p14, 1'b0, O2, O0, O1, n4_to_1_mux_x2_74153_8_p8
  or or_4 (or_4_out, n4_to_1_mux_x2_74153_7_p13, n4_to_1_mux_x2_74153_7_p14);
  // _3_to_8_decoder__74138 #(.Facing("east")) 3_to_8_decoder_74138_2: pin names not known; wires that end beside it: or_4_out, or_3_out, n4_to_1_mux_x2_74153_8_p8, 1'b1, 1'b0, 1'b0, n3_to_8_decoder_74138_2_p7, n3_to_8_decoder_74138_2_p8, n3_to_8_decoder_74138_2_p9, n3_to_8_decoder_74138_2_p10, n3_to_8_decoder_74138_2_p11, n3_to_8_decoder_74138_2_p12, n3_to_8_decoder_74138_2_p13, n3_to_8_decoder_74138_2_p14
  not not_6 (L0, n3_to_8_decoder_74138_2_p7);
  not not_7 (L1, n3_to_8_decoder_74138_2_p8);
  not not_8 (L2, n3_to_8_decoder_74138_2_p9);
  not not_9 (L3, n3_to_8_decoder_74138_2_p10);
  not not_10 (L4, n3_to_8_decoder_74138_2_p11);
  not not_11 (L5, n3_to_8_decoder_74138_2_p12);
  not not_12 (L6, n3_to_8_decoder_74138_2_p13);
  not not_13 (L7, n3_to_8_decoder_74138_2_p14);
endmodule
